# Fritzing sketch Adafruit_9DOF_Accelerometer_Test_Wiring (saved by Fritzing 0.9.2b)
breadboards: 1

parts:
  IMU1 = Adafruit 10-DOF IMU Breakout
  Part1 = Arduino Uno (Rev3)
  R1 = Rotary Potentiometer (Small) [maximum_resistance=100kΩ package=THT]
  R2 = Resistor [tolerance=±5% resistance=1k package=THT]

nets:
  VIN: IMU1.VIN, Part1.5V, R2.Pin_0
  GND: IMU1.GND, Part1.GND
  N1: IMU1.SCL, Part1.A5/SCL
  N2: IMU1.SDA, Part1.A4/SDA
  N3: IMU1.LIN1, Part1.D2
  N4: Part1.A0, R1.leg1, R2.Pin_1
